# Fritzing sketch XIAO-IMU-MPU6050 (saved by Fritzing 0.9.9b)
breadboards: 1

parts:
  A2 = XIAO NRF52840 sense tht
  Part1 = InvenSense MPU6050

nets:
  N1: A2.Pin_2, A2.Pin_21, Part1.GND
  N2: A2.Pin_9, Part1.SDA
  N3: A2.Pin_10, Part1.SCL
  N4: A2.Pin_20, Part1.VCC

custom parts:
  XIAO NRF52840 sense tht: The Seeed Studio XIAO family, Seeed Studio XIAO nRF52840 is equipped with a powerful Nordic nRF52840 MCU which integrates Bluetooth 5.0 connectivity. This is the THT version there is also a SMD version of the part.
